# Fritzing sketch 7-segments_display (saved by Fritzing 0.9.2b)
breadboards: 1

parts:
  U1 = 74HC595 SMD [package="SO16 [SMD]"]
  R6 = Resistor [tolerance=±5% resistance=220 package=THT]
  Raspberry_Pi1 = Raspberry Pi B+
  DI1 = 7-Segment LED Display [package=THT]
  U2 = 74HC595 SMD [package="SO16 [SMD]"]
  R7 = Resistor [tolerance=±5% resistance=220 package=THT]
  DI3 = 7-Segment LED Display [package=THT]

nets:
  N1: U1.Q1, DI1.cathodeB
  N2: U1.Q2, DI1.cathodeC
  N3: U1.Q3, DI1.cathodeD
  N4: U1.Q4, DI1.cathodeE
  N5: U1.Q5, DI1.cathodeF
  N6: U1.Q6, DI1.cathodeG
  N7: U1.Q7, DI1.cathodeDP
  GND: U1.GND, U1.OE, R6.Pin_1, Raspberry_Pi1.GND, U2.GND, U2.OE, R7.Pin_1
  N8: U1.Q7', U2.DS
  VCC: U1.MR, U1.VCC, Raspberry_Pi1.5V, U2.MR, U2.VCC
  N9: U1.SH_CP, Raspberry_Pi1.GPIO27, U2.SH_CP
  N10: U1.ST_CP, Raspberry_Pi1.GPIO18, U2.ST_CP
  N11: U1.DS, Raspberry_Pi1.GPIO17
  N12: U1.Q0, DI1.cathodeA
  N13: R6.Pin_0, DI1.commAnode#2
  N14: U2.Q1, DI3.cathodeB
  N15: U2.Q2, DI3.cathodeC
  N16: U2.Q3, DI3.cathodeD
  N17: U2.Q4, DI3.cathodeE
  N18: U2.Q5, DI3.cathodeF
  N19: U2.Q6, DI3.cathodeG
  N20: U2.Q7, DI3.cathodeDP
  N21: U2.Q0, DI3.cathodeA
  N22: R7.Pin_0, DI3.commAnode#2
