# Fritzing sketch flowing_leds (saved by Fritzing 0.9.2b)
breadboards: 1

parts:
  R1 = Resistor [tolerance=±5% resistance=220 package=THT]
  R2 = Resistor [tolerance=±5% resistance=220 package=THT]
  R3 = Resistor [tolerance=±5% resistance=220 package=THT]
  R4 = Resistor [tolerance=±5% resistance=220 package=THT]
  R6 = Resistor [tolerance=±5% resistance=220 package=THT]
  R7 = Resistor [tolerance=±5% resistance=220 package=THT]
  R8 = Resistor [tolerance=±5% resistance=220 package=THT]
  LED6 = LED - 5mm [color="Red (633nm)" package="5 mm [THT]"]
  LED7 = LED - 5mm [color="Red (633nm)" package="5 mm [THT]"]
  LED8 = LED - 5mm [color="Red (633nm)" package="5 mm [THT]"]
  LED9 = LED - 5mm [color="Red (633nm)" package="5 mm [THT]"]
  LED10 = LED - 5mm [color="Red (633nm)" package="5 mm [THT]"]
  LED11 = LED - 5mm [color="Red (633nm)" package="5 mm [THT]"]
  LED12 = LED - 5mm [color="Red (633nm)" package="5 mm [THT]"]
  Raspberry_Pi1 = Raspberry Pi 2
  U1 = 74HC595 [package="DIP16 [THT]"]
  R9 = Resistor [tolerance=±5% resistance=220 package=THT]
  LED13 = LED - 5mm [color="Red (633nm)" package="5 mm [THT]"]

nets:
  N1: R1.Pin_0, U1.Q7
  N2: R1.Pin_1, LED13.anode
  N3: R2.Pin_0, U1.Q6
  N4: R2.Pin_1, LED12.anode
  N5: R3.Pin_0, U1.Q5
  N6: R3.Pin_1, LED11.anode
  N7: R4.Pin_0, U1.Q4
  N8: R4.Pin_1, LED10.anode
  N9: R6.Pin_0, U1.Q2
  N10: R6.Pin_1, LED8.anode
  N11: R7.Pin_0, U1.Q1
  N12: R7.Pin_1, LED7.anode
  N13: R8.Pin_0, U1.Q0
  N14: R8.Pin_1, LED6.anode
  GND: LED6.cathode, LED7.cathode, LED8.cathode, LED9.cathode, LED10.cathode, LED11.cathode, LED12.cathode, Raspberry_Pi1.GND, U1.GND, U1.OE, LED13.cathode
  N15: LED9.anode, R9.Pin_1
  N16: Raspberry_Pi1.GPIO17, U1.DS
  N17: Raspberry_Pi1.GPIO27, U1.SH_CP
  N18: Raspberry_Pi1.GPIO18, U1.ST_CP
  5V: Raspberry_Pi1.5V, U1.MR, U1.VCC
  N19: U1.Q3, R9.Pin_0
