# Fritzing sketch led_button (saved by Fritzing 0.9.2b)
breadboards: 1

parts:
  Raspberry_Pi1 = Raspberry Pi 2
  R1 = Resistor [tolerance=±5% resistance=220 package=THT]
  S1 = Pushbutton [package="[THT]"]
  LED1 = LED - 5mm [color="Red (633nm)" package="5 mm [THT]"]

nets:
  N1: Raspberry_Pi1.GND, R1.Pin_0, S1.Pin_1, S1.Pin_2
  N2: Raspberry_Pi1.GPIO17, LED1.anode
  N3: Raspberry_Pi1.GPIO18, S1.Pin_3, S1.Pin_4
  N4: R1.Pin_1, LED1.cathode
